# Fritzing sketch scheme (saved by Fritzing 0.9.3b)

parts:
  S2 = H-Bridge with L298N
  U6 = TCRT5000 Line Tracker
  U7 = TCRT5000 Line Tracker
  U8 = TCRT5000 Line Tracker
  Часть4 = SRF05 Ultrasonic Rangefinder
  M3 = DC Motor
  M4 = DC Motor
  RE3 = Rotary Encoder [package=THT]
  RE4 = Rotary Encoder [package=THT]
  LCD2 = LCD MELT screen [part_number=MT-16S2H]
  Часть3 = Arduino Leonardo (Rev3b)
  J2 = Basic Servo

nets:
  12V: S2.12V, Часть3.VIN
  N1: S2.IN1, Часть3.D10_PWM/A10
  N2: S2.IN2, Часть3.D9_PWM/A9
  N3: S2.IN3, Часть3.D6_PWM/A7
  N4: S2.IN4, Часть3.D5_PWM
  N5: S2.M1-01, M3.pin_2
  N6: S2.M1-02, M3.pin_1
  N7: S2.M2-01, M4.pin_2
  N8: S2.M2-02, M4.pin_1
  N9: U6.Ao, Часть3.A0
  N10: U7.Ao, Часть3.A1
  N11: U8.Do, Часть3.D11_PWM
  N12: Часть4.Trig, Часть3.D7
  N13: Часть4.Echo, Часть3.D8/A8
  N14: RE3.EncoderPinC, Часть3.D3_PWM/SCL
  N15: RE4.EncoderPinC, Часть3.D2/SDA
  VDD: LCD2.VDD, Часть3.5V, J2.vcc
  N16: LCD2.RS, Часть3.D12/A11
  GND: LCD2.R/W, Часть3.GND, J2.gnd
  N17: LCD2.E, Часть3.D13_PWM
  N18: LCD2.DB4, Часть3.A2
  N19: LCD2.DB5, Часть3.A3
  N20: LCD2.DB6, Часть3.A4
  N21: LCD2.DB7, Часть3.A5
  N22: Часть3.D4/A6, J2.pulse

custom parts:
  H-Bridge with L298N: h-bridge
  TCRT5000 Line Tracker: A line tracker module based on TCRT5000 (Vishay)
  LCD MELT screen: A standard character display, usually with 2x16 characters. Comes in many colors.
